// Logisim project Anika_simple_as_possible_auto.circ as structural Verilog: 14 circuits, main circuit main
module main (
  input  in_1,
  input  in_2,
  input  in_3,
  input  in_4,
  output [3:0] out_5,
  output [7:0] out_6,
  output [1:0] out_7,
  output [7:0] out_8,
  output [7:0] out_9,
  output [7:0] out_10,
  output [7:0] out_11,
  output [7:0] out_12,
  output [7:0] out_13,
  output [7:0] out_14,
  output [7:0] out_15,
  output [7:0] out_16,
  output [7:0] out_17,
  output [7:0] out_18,
  output [7:0] out_19,
  output [7:0] out_20,
  output [7:0] out_21,
  output [7:0] out_22,
  output [7:0] out_23,
  output [7:0] out_24,
  output [3:0] out_25,
  output [3:0] out_26,
  output [7:0] out_27
);

  wire a_in, a_out, alu_1_alu_carry_out, alu_out, alu_sub, b_in, b_out, flag_en, halt, ins_reg_in_en,
       ins_reg_out_en, jc, jmp_en, jz, mar_in_en, p1, p2, pc_en, pc_out, sram_rd, sram_wr;
  wire [3:0] rom_address;
  wire [7:0] debug_data, multiplexer_1_out;
  wire [7:4] undriven;

  Multiplexer #(.width(8)) multiplexer_1 (
    .in0({out_27[7:4], out_25}), .in1({undriven, rom_address}), .out(multiplexer_1_out), .sel(in_3));
  Hex_Digit_Display hex_digit_display_1 (.value(out_5));  // open: dp
  pc_jump pc_jump_1 (
    .load_or_count(in_1), .pc_reset(jmp_en), .pc_en(pc_en), .clk(in_2), .jumpto(out_25), .pc_out_en(pc_out),
    .pc_value(out_5), .pc_out(out_25));
  sram sram_1 (
    .sram_rd(sram_rd), .sram_wr(sram_wr), .sram_d_in({out_27[7:4], out_25}), .mar_d_in(multiplexer_1_out),
    .mar_in_en(mar_in_en), .sram_clk(in_2), .sram_d_out({out_27[7:4], out_25}), .out_8(out_8), .out_9(out_9),
    .out_10(out_10), .out_11(out_11), .out_12(out_12), .out_13(out_13), .out_14(out_15), .out_15(out_16),
    .out_16(out_17), .out_17(out_18), .out_18(out_19), .out_19(out_20), .out_20(out_21), .out_21(out_22),
    .out_22(out_23), .out_23(out_24));
  boot_loader boot_loader_1 (
    .boot_reset(in_1), .boot_enable(p2), .clk(in_2), .debug(in_3), .rom_address(rom_address), .p1(p1), .p2(p2));
  ROM #(.addrWidth(4)) rom_1 (.addr(rom_address), .data(debug_data));
  assign {out_27[7:4], out_25} = in_3 ? debug_data : 8'bz;  // Controlled_Buffer controlled_buffer_1
  reg_gp reg_gp_1 (
    .reg_in({out_27[7:4], out_25}), .reg_in_en(b_in), .reg_clk(in_2), .reg_out_en(b_out),
    .reg_int_out(out_14), .reg_out({out_27[7:4], out_25}));
  Hex_Digit_Display RegisterA (.value(out_6[7:4]));  // open: dp
  Hex_Digit_Display hex_digit_display_2 (.value(out_6[3:0]));  // open: dp
  reg_gp reg_gp_2 (
    .reg_in({out_27[7:4], out_25}), .reg_in_en(a_in), .reg_clk(in_2), .reg_out_en(a_out),
    .reg_int_out(out_6), .reg_out({out_27[7:4], out_25}));
  ins_reg ins_reg_1 (
    .ins_reg_in({out_27[7:4], out_25}), .ins_reg_in_en(ins_reg_in_en), .clk(in_2),
    .ins_reg_out_en(ins_reg_out_en), .add_outs(out_25), .ins_out(out_26));
  Hex_Digit_Display hex_digit_display_3 (.value(out_14[7:4]));  // open: dp
  alu alu_1 (
    .alu_in_1(out_6), .alu_out_en(alu_out), .alu_sub(alu_sub), .alu_in_2(out_14),
    .alu_carry_out(alu_1_alu_carry_out), .alu_out({out_27[7:4], out_25}));
  Hex_Digit_Display hex_digit_display_4 (.value(out_14[3:0]));  // open: dp
  flag flag_1 (
    .flag_en(flag_en), .clk(in_2), .alu_carry(alu_1_alu_carry_out), .alu_out({out_27[7:4], out_25}), .jc(jc),
    .jz(jz), .flag_out(out_7));
  control_sequencer control_sequencer_1 (
    .cs_en(in_4), .clk(in_2), .ins_out(out_26), .p1(p1), .debug(in_3), .p2(p2), .jz(jz), .jc(jc),
    .mar_in_en(mar_in_en), .sram_rd(sram_rd), .ins_reg_in_en(ins_reg_in_en), .ins_reg_out_en(ins_reg_out_en),
    .a_in(a_in), .pc_out(pc_out), .sram_wr(sram_wr), .a_out(a_out), .b_in(b_in), .halt(halt), .pc_en(pc_en),
    .flag_en(flag_en), .alu_out(alu_out), .jmp_en(jmp_en));

  assign out_27[3:0] = out_25;

  // Other names for the same wires on the sheet: clk = in_2; debug = in_3; jmpto[3:0] = out_25; pc_reset = in_1

  // Notes on the sheet:
  //   contents of rom_1 (hex, n*v repeats v):
  //   1d 2e 30 5f f0 8*0 19 f
  //   Register A
  //   Register B
endmodule

module reg_gp (
  input  [7:0] reg_in,
  input  reg_in_en,
  input  reg_clk,
  input  reg_out_en,
  output [7:0] reg_int_out,
  output [7:0] reg_out
);

  wire multiplexer_1_out, multiplexer_2_out, multiplexer_3_out, multiplexer_4_out, multiplexer_5_out,
       multiplexer_6_out, multiplexer_7_out, multiplexer_8_out;

  Multiplexer multiplexer_1 (.in0(reg_int_out[7]), .in1(reg_in[7]), .out(multiplexer_1_out), .sel(reg_in_en));
  D_Flip_Flop d_ff_1 (.D(multiplexer_1_out), .clk(reg_clk), .Q(reg_int_out[7]));  // open: Qn, preset, reset
  assign reg_out[7] = reg_out_en ? reg_int_out[7] : 1'bz;  // Controlled_Buffer controlled_buffer_1
  Multiplexer multiplexer_2 (.in0(reg_int_out[6]), .in1(reg_in[6]), .out(multiplexer_2_out), .sel(reg_in_en));
  D_Flip_Flop d_ff_2 (.D(multiplexer_2_out), .clk(reg_clk), .Q(reg_int_out[6]));  // open: Qn, preset, reset
  Multiplexer multiplexer_3 (.in0(reg_int_out[5]), .in1(reg_in[5]), .out(multiplexer_3_out), .sel(reg_in_en));
  assign reg_out[6] = reg_out_en ? reg_int_out[6] : 1'bz;  // Controlled_Buffer controlled_buffer_2
  D_Flip_Flop d_ff_3 (.D(multiplexer_3_out), .clk(reg_clk), .Q(reg_int_out[5]));  // open: Qn, preset, reset
  Multiplexer multiplexer_4 (.in0(reg_int_out[4]), .in1(reg_in[4]), .out(multiplexer_4_out), .sel(reg_in_en));
  assign reg_out[5] = reg_out_en ? reg_int_out[5] : 1'bz;  // Controlled_Buffer controlled_buffer_3
  D_Flip_Flop d_ff_4 (.D(multiplexer_4_out), .clk(reg_clk), .Q(reg_int_out[4]));  // open: Qn, preset, reset
  Multiplexer multiplexer_5 (.in0(reg_int_out[3]), .in1(reg_in[3]), .out(multiplexer_5_out), .sel(reg_in_en));
  assign reg_out[4] = reg_out_en ? reg_int_out[4] : 1'bz;  // Controlled_Buffer controlled_buffer_4
  D_Flip_Flop d_ff_5 (.D(multiplexer_5_out), .clk(reg_clk), .Q(reg_int_out[3]));  // open: Qn, preset, reset
  Multiplexer multiplexer_6 (.in0(reg_int_out[2]), .in1(reg_in[2]), .out(multiplexer_6_out), .sel(reg_in_en));
  D_Flip_Flop d_ff_6 (.D(multiplexer_6_out), .clk(reg_clk), .Q(reg_int_out[2]));  // open: Qn, preset, reset
  assign reg_out[3] = reg_out_en ? reg_int_out[3] : 1'bz;  // Controlled_Buffer controlled_buffer_5
  assign reg_out[2] = reg_out_en ? reg_int_out[2] : 1'bz;  // Controlled_Buffer controlled_buffer_6
  Multiplexer multiplexer_7 (.in0(reg_int_out[1]), .in1(reg_in[1]), .out(multiplexer_7_out), .sel(reg_in_en));
  D_Flip_Flop d_ff_7 (.D(multiplexer_7_out), .clk(reg_clk), .Q(reg_int_out[1]));  // open: Qn, preset, reset
  assign reg_out[1] = reg_out_en ? reg_int_out[1] : 1'bz;  // Controlled_Buffer controlled_buffer_7
  Multiplexer multiplexer_8 (.in0(reg_int_out[0]), .in1(reg_in[0]), .out(multiplexer_8_out), .sel(reg_in_en));
  D_Flip_Flop d_ff_8 (.D(multiplexer_8_out), .clk(reg_clk), .Q(reg_int_out[0]));  // open: Qn, preset, reset
  assign reg_out[0] = reg_out_en ? reg_int_out[0] : 1'bz;  // Controlled_Buffer controlled_buffer_8

  // Notes on the sheet:
  //   Input
  //   Input Control
  //   Clock
  //   Output Control
  //   Memory
  //   Internal Output
  //   Output
endmodule

module alu (
  input  [7:0] alu_in_1,
  input  alu_out_en,
  input  alu_sub,
  input  [7:0] alu_in_2,
  output alu_carry_out,
  output [7:0] alu_out
);

  wire adder_2_cout, adder_3_cout, adder_4_cout, adder_5_cout, adder_6_cout, adder_7_cout, adder_8_cout,
       xor_1_out, xor_2_out, xor_3_out, xor_4_out, xor_5_out, xor_6_out, xor_7_out, xor_8_out;
  wire [7:0] adder_8_out;

  Adder #(.width(1)) adder_1 (
    .a(alu_in_1[7]), .b(xor_1_out), .out(adder_8_out[7]), .cin(adder_2_cout), .cout(alu_carry_out));
  xor xor_1 (xor_1_out, alu_in_2[7], alu_sub);
  Adder #(.width(1)) adder_2 (
    .a(alu_in_1[6]), .b(xor_2_out), .out(adder_8_out[6]), .cin(adder_3_cout), .cout(adder_2_cout));
  xor xor_2 (xor_2_out, alu_in_2[6], alu_sub);
  Adder #(.width(1)) adder_3 (
    .a(alu_in_1[5]), .b(xor_3_out), .out(adder_8_out[5]), .cin(adder_4_cout), .cout(adder_3_cout));
  xor xor_3 (xor_3_out, alu_in_2[5], alu_sub);
  Adder #(.width(1)) adder_4 (
    .a(alu_in_1[4]), .b(xor_4_out), .out(adder_8_out[4]), .cin(adder_5_cout), .cout(adder_4_cout));
  xor xor_4 (xor_4_out, alu_in_2[4], alu_sub);
  Adder #(.width(1)) adder_5 (
    .a(alu_in_1[3]), .b(xor_5_out), .out(adder_8_out[3]), .cin(adder_6_cout), .cout(adder_5_cout));
  xor xor_5 (xor_5_out, alu_in_2[3], alu_sub);
  Adder #(.width(1)) adder_6 (
    .a(alu_in_1[2]), .b(xor_6_out), .out(adder_8_out[2]), .cin(adder_7_cout), .cout(adder_6_cout));
  xor xor_6 (xor_6_out, alu_in_2[2], alu_sub);
  Adder #(.width(1)) adder_7 (
    .a(alu_in_1[1]), .b(xor_7_out), .out(adder_8_out[1]), .cin(adder_8_cout), .cout(adder_7_cout));
  xor xor_7 (xor_7_out, alu_in_2[1], alu_sub);
  Adder #(.width(1)) adder_8 (.a(alu_in_1[0]), .b(xor_8_out), .out(adder_8_out[0]), .cin(alu_sub), .cout(adder_8_cout));
  xor xor_8 (xor_8_out, alu_in_2[0], alu_sub);
  assign alu_out = alu_out_en ? adder_8_out : 8'bz;  // Controlled_Buffer controlled_buffer_1

  // Notes on the sheet:
  //   Input 1
  //   Carry Output
  //   Subtract Control
  //   Full Adders
  //   Input 2
  //   Output Control
  //   ALU Output
endmodule

module pc (
  input  pc_en,
  input  pc_clk,
  input  pc_reset,
  input  pc_out_en,
  output [3:0] pc_value,
  output [3:0] pc_out
);

  wire j_k_ff_2_qn, j_k_ff_3_qn, j_k_ff_4_qn;

  J_K_Flip_Flop j_k_ff_1 (
    .J(pc_en), .K(pc_en), .clk(j_k_ff_2_qn), .Q(pc_value[3]), .reset(pc_reset));  // open: Qn, preset
  J_K_Flip_Flop j_k_ff_2 (
    .J(pc_en), .K(pc_en), .clk(j_k_ff_3_qn), .Q(pc_value[2]), .Qn(j_k_ff_2_qn), .reset(pc_reset));  // open: preset
  J_K_Flip_Flop j_k_ff_3 (
    .J(pc_en), .K(pc_en), .clk(j_k_ff_4_qn), .Q(pc_value[1]), .Qn(j_k_ff_3_qn), .reset(pc_reset));  // open: preset
  J_K_Flip_Flop j_k_ff_4 (
    .J(pc_en), .K(pc_en), .clk(pc_clk), .Q(pc_value[0]), .Qn(j_k_ff_4_qn), .reset(pc_reset));  // open: preset
  assign pc_out = pc_out_en ? pc_value : 4'bz;  // Controlled_Buffer controlled_buffer_1

  // Notes on the sheet:
  //   Clock
  //   Reset
  //   Output Control
  //   Count Control
  //   Counter Output
endmodule

module dec_4x16 (
  input  [3:0] dec_sel,
  output [15:0] dec_out
);

  wire not_1_out, not_2_out, not_3_out, not_4_out;

  not not_1 (not_1_out, dec_sel[3]);
  not not_2 (not_2_out, dec_sel[2]);
  not not_3 (not_3_out, dec_sel[1]);
  not not_4 (not_4_out, dec_sel[0]);
  and and_1 (dec_out[0], not_4_out, not_3_out, not_2_out, not_1_out);
  and and_2 (dec_out[1], dec_sel[0], not_3_out, not_2_out, not_1_out);
  and and_3 (dec_out[2], not_4_out, dec_sel[1], not_2_out, not_1_out);
  and and_4 (dec_out[3], dec_sel[0], dec_sel[1], not_2_out, not_1_out);
  and and_5 (dec_out[4], not_4_out, not_3_out, dec_sel[2], not_1_out);
  and and_6 (dec_out[5], dec_sel[0], not_3_out, dec_sel[2], not_1_out);
  and and_7 (dec_out[6], not_4_out, dec_sel[1], dec_sel[2], not_1_out);
  and and_8 (dec_out[7], dec_sel[0], dec_sel[1], dec_sel[2], not_1_out);
  and and_9 (dec_out[8], not_4_out, not_3_out, not_2_out, dec_sel[3]);
  and and_10 (dec_out[9], dec_sel[0], not_3_out, not_2_out, dec_sel[3]);
  and and_11 (dec_out[10], not_4_out, dec_sel[1], not_2_out, dec_sel[3]);
  and and_12 (dec_out[11], dec_sel[0], dec_sel[1], not_2_out, dec_sel[3]);
  and and_13 (dec_out[12], not_4_out, not_3_out, dec_sel[2], dec_sel[3]);
  and and_14 (dec_out[13], dec_sel[0], not_3_out, dec_sel[2], dec_sel[3]);
  and and_15 (dec_out[14], not_4_out, dec_sel[1], dec_sel[2], dec_sel[3]);
  and and_16 (dec_out[15], dec_sel[0], dec_sel[1], dec_sel[2], dec_sel[3]);
endmodule

module sram_cell (
  input  [7:0] data_in,
  input  wr_en,
  input  clk,
  input  cs,
  input  rd_en,
  output [7:0] memory_content,
  output [7:0] data_out
);

  wire and_1_out, and_2_out;

  and and_1 (and_1_out, wr_en, cs);
  and and_2 (and_2_out, cs, rd_en);
  reg_gp reg_gp_1 (
    .reg_in(data_in), .reg_in_en(and_1_out), .reg_clk(clk), .reg_out_en(and_2_out),
    .reg_int_out(memory_content), .reg_out(data_out));
endmodule

module sram (
  input  sram_rd,
  input  sram_wr,
  input  [7:0] sram_d_in,
  input  [7:0] mar_d_in,
  input  mar_in_en,
  input  sram_clk,
  output [7:0] sram_d_out,
  output [7:0] out_8,
  output [7:0] out_9,
  output [7:0] out_10,
  output [7:0] out_11,
  output [7:0] out_12,
  output [7:0] out_13,
  output [7:0] out_14,
  output [7:0] out_15,
  output [7:0] out_16,
  output [7:0] out_17,
  output [7:0] out_18,
  output [7:0] out_19,
  output [7:0] out_20,
  output [7:0] out_21,
  output [7:0] out_22,
  output [7:0] out_23
);

  wire [7:0] controlled_buffer_1_out, reg_gp_1_reg_int_out;
  wire [15:0] dec_4x16_1_dec_out;

  reg_gp reg_gp_1 (
    .reg_in(mar_d_in), .reg_in_en(mar_in_en), .reg_clk(sram_clk), .reg_int_out(reg_gp_1_reg_int_out));  // open: reg_out_en, reg_out
  dec_4x16 dec_4x16_1 (.dec_sel(reg_gp_1_reg_int_out[3:0]), .dec_out(dec_4x16_1_dec_out));
  assign controlled_buffer_1_out = sram_wr ? sram_d_in : 8'bz;  // Controlled_Buffer controlled_buffer_1
  sram_cell sram_cell_1 (
    .data_in(controlled_buffer_1_out), .wr_en(sram_wr), .clk(sram_clk), .cs(dec_4x16_1_dec_out[0]),
    .rd_en(sram_rd), .memory_content(out_8), .data_out(controlled_buffer_1_out));
  sram_cell sram_cell_2 (
    .data_in(controlled_buffer_1_out), .wr_en(sram_wr), .clk(sram_clk), .cs(dec_4x16_1_dec_out[1]),
    .rd_en(sram_rd), .memory_content(out_9), .data_out(controlled_buffer_1_out));
  sram_cell sram_cell_3 (
    .data_in(controlled_buffer_1_out), .wr_en(sram_wr), .clk(sram_clk), .cs(dec_4x16_1_dec_out[2]),
    .rd_en(sram_rd), .memory_content(out_10), .data_out(controlled_buffer_1_out));
  sram_cell sram_cell_4 (
    .data_in(controlled_buffer_1_out), .wr_en(sram_wr), .clk(sram_clk), .cs(dec_4x16_1_dec_out[3]),
    .rd_en(sram_rd), .memory_content(out_11), .data_out(controlled_buffer_1_out));
  sram_cell sram_cell_5 (
    .data_in(controlled_buffer_1_out), .wr_en(sram_wr), .clk(sram_clk), .cs(dec_4x16_1_dec_out[4]),
    .rd_en(sram_rd), .memory_content(out_12), .data_out(controlled_buffer_1_out));
  sram_cell sram_cell_6 (
    .data_in(controlled_buffer_1_out), .wr_en(sram_wr), .clk(sram_clk), .cs(dec_4x16_1_dec_out[5]),
    .rd_en(sram_rd), .memory_content(out_13), .data_out(controlled_buffer_1_out));
  sram_cell sram_cell_7 (
    .data_in(controlled_buffer_1_out), .wr_en(sram_wr), .clk(sram_clk), .cs(dec_4x16_1_dec_out[6]),
    .rd_en(sram_rd), .memory_content(out_14), .data_out(controlled_buffer_1_out));
  sram_cell sram_cell_8 (
    .data_in(controlled_buffer_1_out), .wr_en(sram_wr), .clk(sram_clk), .cs(dec_4x16_1_dec_out[7]),
    .rd_en(sram_rd), .memory_content(out_15), .data_out(controlled_buffer_1_out));
  sram_cell sram_cell_9 (
    .data_in(controlled_buffer_1_out), .wr_en(sram_wr), .clk(sram_clk), .cs(dec_4x16_1_dec_out[8]),
    .rd_en(sram_rd), .memory_content(out_16), .data_out(controlled_buffer_1_out));
  sram_cell sram_cell_10 (
    .data_in(controlled_buffer_1_out), .wr_en(sram_wr), .clk(sram_clk), .cs(dec_4x16_1_dec_out[9]),
    .rd_en(sram_rd), .memory_content(out_17), .data_out(controlled_buffer_1_out));
  sram_cell sram_cell_11 (
    .data_in(controlled_buffer_1_out), .wr_en(sram_wr), .clk(sram_clk), .cs(dec_4x16_1_dec_out[10]),
    .rd_en(sram_rd), .memory_content(out_18), .data_out(controlled_buffer_1_out));
  sram_cell sram_cell_12 (
    .data_in(controlled_buffer_1_out), .wr_en(sram_wr), .clk(sram_clk), .cs(dec_4x16_1_dec_out[11]),
    .rd_en(sram_rd), .memory_content(out_19), .data_out(controlled_buffer_1_out));
  sram_cell sram_cell_13 (
    .data_in(controlled_buffer_1_out), .wr_en(sram_wr), .clk(sram_clk), .cs(dec_4x16_1_dec_out[12]),
    .rd_en(sram_rd), .memory_content(out_20), .data_out(controlled_buffer_1_out));
  sram_cell sram_cell_14 (
    .data_in(controlled_buffer_1_out), .wr_en(sram_wr), .clk(sram_clk), .cs(dec_4x16_1_dec_out[13]),
    .rd_en(sram_rd), .memory_content(out_21), .data_out(controlled_buffer_1_out));
  sram_cell sram_cell_15 (
    .data_in(controlled_buffer_1_out), .wr_en(sram_wr), .clk(sram_clk), .cs(dec_4x16_1_dec_out[14]),
    .rd_en(sram_rd), .memory_content(out_22), .data_out(controlled_buffer_1_out));
  sram_cell sram_cell_16 (
    .data_in(controlled_buffer_1_out), .wr_en(sram_wr), .clk(sram_clk), .cs(dec_4x16_1_dec_out[15]),
    .rd_en(sram_rd), .memory_content(out_23), .data_out(controlled_buffer_1_out));
  assign sram_d_out = sram_rd ? controlled_buffer_1_out : 8'bz;  // Controlled_Buffer controlled_buffer_2
endmodule

module ins_reg (
  input  [7:0] ins_reg_in,
  input  ins_reg_in_en,
  input  clk,
  input  ins_reg_out_en,
  output [3:0] add_outs,
  output [3:0] ins_out
);

  wire [3:0] reg_gp_1_reg_int_out;

  reg_gp reg_gp_1 (
    .reg_in(ins_reg_in), .reg_in_en(ins_reg_in_en), .reg_clk(clk),
    .reg_int_out({ins_out, reg_gp_1_reg_int_out}));  // open: reg_out_en, reg_out
  assign add_outs = ins_reg_out_en ? reg_gp_1_reg_int_out : 4'bz;  // Controlled_Buffer controlled_buffer_1
endmodule

module ring_counter (
  input  rc_en,
  input  clk,
  output T1,
  output T2,
  output T3,
  output T4,
  output T5,
  output T6
);

  wire [3:0] counter_1_q;
  wire [15:6] dec_4x16_1_dec_out;

  Counter #(.max('hf), .width(4)) counter_1 (
    .clr(dec_4x16_1_dec_out[6]), .load(1'b0), .up(1'b1), .count(rc_en), .clk(clk), .Q(counter_1_q));  // open: D, carry
  dec_4x16 dec_4x16_1 (.dec_sel(counter_1_q), .dec_out({dec_4x16_1_dec_out, T6, T5, T4, T3, T2, T1}));
endmodule

module ins_dec (
  input  [3:0] ins_out,
  output LDA,
  output LDB,
  output ADD,
  output STA,
  output JMP,
  output HLT,
  output JZ,
  output JC
);

  wire [15:0] dec_4x16_1_dec_out;

  dec_4x16 dec_4x16_1 (
    .dec_sel(ins_out),
    .dec_out({dec_4x16_1_dec_out[15:9], JC, JZ, HLT, JMP, STA, ADD, LDB, LDA, dec_4x16_1_dec_out[0]}));
endmodule

module control_sequencer (
  input  cs_en,
  input  clk,
  input  [3:0] ins_out,
  input  p1,
  input  debug,
  input  p2,
  input  jz,
  input  jc,
  output mar_in_en,
  output sram_rd,
  output ins_reg_in_en,
  output ins_reg_out_en,
  output a_in,
  output pc_out,
  output sram_wr,
  output a_out,
  output b_in,
  output halt,
  output pc_en,
  output flag_en,
  output alu_out,
  output jmp_en
);

  wire and_1_out, and_3_out, and_4_out, and_5_out, and_6_out, and_8_out, and_10_out, and_11_out, and_13_out,
       and_14_out, and_15_out, and_17_out, and_18_out, and_19_out, and_20_out, and_21_out, and_23_out,
       and_25_out, and_27_out, and_28_out, and_30_out, and_32_out, ins_dec_1_add, ins_dec_1_hlt,
       ins_dec_1_jc, ins_dec_1_jmp, ins_dec_1_jz, ins_dec_1_lda, ins_dec_1_ldb, ins_dec_1_sta, not_1_out,
       or_1_out, or_2_out, or_3_out, or_4_out, or_5_out, ring_counter_1_t1, ring_counter_1_t2,
       ring_counter_1_t4, ring_counter_1_t5;

  ins_dec ins_dec_1 (
    .ins_out(ins_out), .LDA(ins_dec_1_lda), .LDB(ins_dec_1_ldb), .ADD(ins_dec_1_add), .STA(ins_dec_1_sta),
    .JMP(ins_dec_1_jmp), .HLT(ins_dec_1_hlt), .JZ(ins_dec_1_jz), .JC(ins_dec_1_jc));
  ring_counter ring_counter_1 (
    .rc_en(cs_en), .clk(clk), .T1(ring_counter_1_t1), .T2(ring_counter_1_t2), .T3(pc_en),
    .T4(ring_counter_1_t4), .T5(ring_counter_1_t5));  // open: T6
  and and_1 (and_1_out, pc_en, ins_dec_1_jmp);
  not not_1 (not_1_out, debug);
  and and_2 (pc_out, ring_counter_1_t1, not_1_out);
  and and_3 (and_3_out, ring_counter_1_t4, ins_dec_1_lda);
  or or_1 (or_1_out, ring_counter_1_t1, and_3_out, and_4_out, and_5_out);
  Multiplexer multiplexer_1 (.in0(or_1_out), .in1(p1), .out(mar_in_en), .sel(debug));
  and and_4 (and_4_out, ring_counter_1_t4, ins_dec_1_ldb);
  and and_5 (and_5_out, ring_counter_1_t4, ins_dec_1_sta);
  and and_6 (and_6_out, jz, ins_dec_1_jz, pc_en);
  or or_2 (or_2_out, and_1_out, and_6_out, and_20_out);
  and and_7 (jmp_en, not_1_out, or_2_out);
  and and_8 (and_8_out, ring_counter_1_t5, ins_dec_1_lda);
  or or_3 (or_3_out, ring_counter_1_t2, and_8_out, and_10_out);
  and and_9 (sram_rd, or_3_out, not_1_out);
  and and_10 (and_10_out, ring_counter_1_t5, ins_dec_1_ldb);
  and and_11 (and_11_out, ins_dec_1_jc, pc_en);
  and and_12 (ins_reg_in_en, ring_counter_1_t2, not_1_out);
  and and_13 (and_13_out, ring_counter_1_t4, ins_dec_1_lda);
  and and_14 (and_14_out, pc_en, ins_dec_1_jz);
  and and_15 (and_15_out, ring_counter_1_t4, ins_dec_1_ldb);
  or or_4 (or_4_out, and_11_out, and_14_out, and_13_out, and_15_out, and_17_out, and_18_out);
  and and_16 (ins_reg_out_en, or_4_out, not_1_out);
  and and_17 (and_17_out, ring_counter_1_t4, ins_dec_1_sta);
  and and_18 (and_18_out, pc_en, ins_dec_1_jmp);
  and and_19 (and_19_out, ring_counter_1_t5, ins_dec_1_lda);
  or or_5 (or_5_out, and_19_out, and_21_out);
  and and_20 (and_20_out, jc, ins_dec_1_jc, pc_en);
  and and_21 (and_21_out, ring_counter_1_t4, ins_dec_1_add);
  and and_22 (a_in, or_5_out, not_1_out);
  and and_23 (and_23_out, ring_counter_1_t5, ins_dec_1_sta);
  and and_24 (a_out, and_23_out, not_1_out);
  and and_25 (and_25_out, ring_counter_1_t5, ins_dec_1_ldb);
  and and_26 (b_in, and_25_out, not_1_out);
  and and_27 (and_27_out, ring_counter_1_t4, ins_dec_1_add);
  and and_28 (and_28_out, ring_counter_1_t5, ins_dec_1_sta);
  Multiplexer multiplexer_2 (.in0(and_28_out), .in1(p2), .out(sram_wr), .sel(debug));
  and and_29 (alu_out, and_27_out, not_1_out);
  and and_30 (and_30_out, ring_counter_1_t4, ins_dec_1_hlt);
  and and_31 (halt, and_30_out, not_1_out);
  and and_32 (and_32_out, ring_counter_1_t4, ins_dec_1_add);
  and and_33 (flag_en, and_32_out, not_1_out);
endmodule

module boot_loader (
  input  boot_reset,
  input  boot_enable,
  input  clk,
  input  debug,
  output [3:0] rom_address,
  output p1,
  output p2
);

  wire controlled_buffer_1_out, d_ff_1_q, not_1_out;

  D_Flip_Flop d_ff_1 (.D(controlled_buffer_1_out), .clk(clk), .Q(d_ff_1_q));  // open: Qn, preset, reset
  assign controlled_buffer_1_out = debug ? not_1_out : 1'bz;  // Controlled_Buffer controlled_buffer_1
  Counter #(.max('hf), .width(4)) counter_1 (
    .clr(boot_reset), .load(1'b0), .up(1'b1), .count(boot_enable), .clk(clk), .Q(rom_address));  // open: D, carry
  not not_1 (not_1_out, d_ff_1_q);
  and and_1 (p1, not_1_out, debug);
  and and_2 (p2, d_ff_1_q, debug);
endmodule

module pc_jump (
  input  load_or_count,
  input  pc_reset,
  input  pc_en,
  input  clk,
  input  [3:0] jumpto,
  input  pc_out_en,
  output [3:0] pc_value,
  output [3:0] pc_out
);

  Counter #(.max('hf), .width(4)) counter_1 (
    .clr(pc_reset), .load(load_or_count), .up(1'b1), .count(pc_en), .clk(clk), .D(jumpto), .Q(pc_value));  // open: carry
  assign pc_out = pc_out_en ? pc_value : 4'bz;  // Controlled_Buffer controlled_buffer_1
endmodule

module flag (
  input  flag_en,
  input  clk,
  input  alu_carry,
  input  [7:0] alu_out,
  output jc,
  output jz,
  output [1:0] flag_out
);

  wire nor_1_out;
  wire [1:1] controlled_buffer_1_out;

  assign controlled_buffer_1_out[1] = flag_en ? nor_1_out : 1'bz;  // Controlled_Buffer controlled_buffer_1
  nor nor_1 (nor_1_out, alu_out[0], alu_out[1], alu_out[2], alu_out[3], alu_out[4], alu_out[5], alu_out[6], alu_out[7]);
  Register #(.width(2)) register_1 (
    .D({controlled_buffer_1_out[1], alu_carry}), .en(flag_en), .clk(clk), .Q(flag_out));  // open: clr

  assign jc = flag_out[0];
  assign jz = flag_out[1];
endmodule
